# Fritzing sketch apis (saved by Fritzing 0.9.3b)
breadboards: 1

parts:
  Part1 = Arduino Uno (Rev3) - ICSP
  M1 = DC Motor
  S1 = Pushbutton [package="[SMD]"]
  S2 = Pushbutton [package="[SMD]"]
  S3 = Pushbutton [package="[SMD]"]
  Part2 = Real Time Clock Module - DS1307 RTC Breakout Board
  IC1 = L293D [package=THT]
  R3 = Resistor [tolerance=±5% resistance=10k package="2512 [SMD]"]
  Part3 = 0.56" 7-segment LED Backpack [part_number=878]
  PART1 = SparkFun Soil Moisture Sensor [part_number=SEN-13322]
  R4 = Resistor [tolerance=±5% resistance=10k package="2512 [SMD]"]
  R5 = Resistor [tolerance=±5% resistance=10k package="2512 [SMD]"]
  PART2 = SparkFun Soil Moisture Sensor [part_number=SEN-13322]

nets:
  N1: Part1.A1, PART1.SIG
  N2: Part1.A2, PART2.VCC
  N3: Part1.A3, PART2.SIG
  N4: Part1.A4/SDA, Part2.SDA, Part3.SDA
  N5: Part1.A5/SCL, Part2.SCL, Part3.SCL
  N6: Part1.D8, S2.Pin_3, S2.Pin_4, R5.Pin_0
  N7: Part1.D9_PWM, S3.Pin_3, S3.Pin_4, R3.Pin_0
  N8: Part1.D10_PWM/SS, PART1.VCC
  GND: Part1.GND, Part2.GND, IC1.0V, R3.Pin_1, Part3.GND, PART1.GND, R4.Pin_1, R5.Pin_1, PART2.GND
  N9: Part1.D2, S1.Pin_3, S1.Pin_4, R4.Pin_0
  N10: Part1.D5_PWM, IC1.Enable_1
  N11: Part1.D6_PWM, IC1.In_1
  N12: Part1.D7, IC1.In_2
  5V: Part1.5V, S1.Pin_1, S1.Pin_2, S2.Pin_1, S2.Pin_2, S3.Pin_1, S3.Pin_2, Part2.5V, IC1.+V, Part3.VDD
  N13: Part1.VIN, IC1.+Vmotor
  N14: M1.pin_1, IC1.Out_1_(_Controlled_by_Enable_1_)
  N15: M1.pin_2, IC1.Out_2_(_Controlled_by_Enable_1_)

notes:
  Buttons:
  SELECT   PLUS   MINUS
  Soil Humidity Detection Sensor Module
  4X Numeric LED Display Digital Tube JY-MCU Module
  DS1307 Real Time Clock breakout board kit
  12V Peristaltic Liquid Pump with Silicone Tubing
  12V for the pump
  Power with 12V
  12V
  5V
  Under the pot leak sensor

custom parts:
  0.56" 7-segment LED Backpack: This 0.56" 7-segment LED display includes a driver chip for simple control via an I2C interface. The backpack features address-selection jumpers so you can connect up to eight displays on a single I2C bus.
  SparkFun Soil Moisture Sensor: The SparkFun Soil Moisture Sensor is a simple breakout for measuring the moisture in soil and similar materials.
